# Fritzing sketch sensor_shield (saved by Fritzing 0.9.3b)
circuit board: 6.9215cm x 5.33756cm
breadboards: 1

parts:
  DGS = female pin header, 8 pins [form="♀ (female)"]
  V2_1 = Arduino Uno (Rev3)
  Fan = female pin header, 2 pins [form="♀ (female)"]
  RFM95W_(Radio) = female pin header, 8 pins [form="♀ (female)"]  # not connected
  1602A_(LCD) = female pin header, 16 pins [form="♀ (female)"]  # not connected
  DS1307_(RTC) = female pin header, 5 pins [form="♀ (female)"]  # not connected

nets:
  N1: DGS.pin2, V2_1.A0
  N2: DGS.pin3, V2_1.A1
  N3: DGS.pin6, V2_1.GND, Fan.pin1
  N4: DGS.pin8, V2_1.3V3
  N5: V2_1.5V, Fan.pin2
